# Fritzing sketch LedTrialShieldBlueBelt (saved by Fritzing 0.8.7b)
circuit board: 16cm x 10cm
breadboards: 2

parts:
  ArduinoKid = Arduino Uno (Rev3)
  ArduinoObserver = Arduino Uno (Rev3)
  J2 = Piezo Speaker
  C1 = Electrolytic Capacitor [capacitance=1mF package="100 mil [THT, electrolytic]"]
  LED1 = LED - 5mm [color="Red (633nm)" package="5 mm [THT]"]
  R1 = Resistor [tolerance=±5% resistance=1k package=THT]

nets:
  N1: ArduinoKid.D9_PWM, ArduinoObserver.A0, C1.+, LED1.anode
  5V: ArduinoKid.5V, ArduinoObserver.5V
  GND: ArduinoKid.GND, ArduinoObserver.GND, J2.pin1, C1.-, R1.Pin_1
  N2: ArduinoObserver.D12/MISO, J2.pin2
  N3: LED1.cathode, R1.Pin_0

notes:
  Kid Arduino
  Observer Arduino
  The LED Trial Shield Blue belt
