# Fritzing sketch LedTrialShieldOrangeBelt (saved by Fritzing 0.8.7b)
circuit board: 16cm x 10cm
breadboards: 2

parts:
  R1 = Resistor [tolerance=±5% resistance=220 package=THT]
  R2 = Resistor [tolerance=±5% resistance=220 package=THT]
  R3 = Resistor [tolerance=±5% resistance=220 package=THT]
  R4 = Resistor [tolerance=±5% resistance=220 package=THT]
  R5 = Resistor [tolerance=±5% resistance=220 package=THT]
  R6 = Resistor [tolerance=±5% resistance=220 package=THT]
  R7 = Resistor [tolerance=±5% resistance=220 package=THT]
  R8 = Resistor [tolerance=±5% resistance=220 package=THT]
  IC1 = IC, DIP package, 14 pins [chip_label=IC]
  ArduinoKid = Arduino Uno (Rev3)
  Part1 = Arduino Uno (Rev3)
  J1 = Piezo Speaker

nets:
  N1: R1.Pin_0, ArduinoKid.D2, Part1.D2
  N2: R1.Pin_1, IC1.pin1
  N3: R2.Pin_0, ArduinoKid.D7, Part1.D7
  N4: R2.Pin_1, IC1.pin2
  N5: R3.Pin_0, ArduinoKid.D6_PWM, Part1.D6_PWM
  N6: R3.Pin_1, IC1.pin7
  N7: R4.Pin_1, IC1.pin6
  N8: R5.Pin_0, IC1.pin10
  N9: R5.Pin_1, ArduinoKid.D4, Part1.D4
  N10: R6.Pin_0, IC1.pin8
  N11: R6.Pin_1, ArduinoKid.D5_PWM, Part1.D5_PWM
  N12: R7.Pin_0, IC1.pin13
  N13: R7.Pin_1, ArduinoKid.D3_PWM, Part1.D3_PWM
  N14: R8.Pin_0, IC1.pin11
  N15: R8.Pin_1, ArduinoKid.D8, Part1.D8
  GND: IC1.pin14, ArduinoKid.GND, Part1.GND, J1.pin1
  5V: ArduinoKid.5V, Part1.5V
  N16: Part1.D12/MISO, J1.pin2

notes:
  This IC is a placeholder for a 7-segment display
  +A+
  F B
  +G+
  E C
  +D+
  1: A
  2: F
  3:
  4:
  5:
  6: Option for left dot
  7: E
  8: D
  9: Right dot
  10: C
  11: G
  12:
  13: B
  14: GND
  Kid Arduino
  Observer Arduino
  The LED Trial Shield Orange belt
