# Fritzing sketch LedTrialShieldYellowBelt (saved by Fritzing 0.8.7b)
circuit board: 16cm x 10cm
breadboards: 1

parts:
  ArduinoStudent = Arduino Uno (Rev3)
  ArduinoObserver = Arduino Uno (Rev3)
  LED1 = LED - 5mm [color="Red (633nm)" package="5 mm [THT]"]
  LED2 = LED - 5mm [color="Red (633nm)" package="5 mm [THT]"]
  LED_SUCCESS = LED - 5mm [color="Green (555nm)" package="5 mm [THT]"]
  R_SUCCESS = Resistor [tolerance=±5% resistance=220 package=THT]
  R2 = Resistor [tolerance=±5% resistance=220 package=THT]
  R1 = Resistor [tolerance=±5% resistance=220 package=THT]

nets:
  N1: ArduinoStudent.D12/MISO, ArduinoObserver.A1, LED2.anode
  N2: ArduinoStudent.D13/SCK, ArduinoObserver.A0, LED1.anode
  GND: ArduinoStudent.GND, ArduinoObserver.GND, R_SUCCESS.Pin_1, R2.Pin_1, R1.Pin_1
  N3: ArduinoObserver.D13/SCK, LED_SUCCESS.anode
  N4: LED1.cathode, R1.Pin_0
  N5: LED2.cathode, R2.Pin_0
  N6: LED_SUCCESS.cathode, R_SUCCESS.Pin_0

notes:
  Observer Arduino
  Will be replaced by Atmega chip
  LED will be replaced
  by a buzzer
